// Logisim project lab exam.circ as structural Verilog: 11 circuits, main circuit main
module main (
  input  [6:0] OPCODE,
  output MEM_WRITE,
  output BRANCH,
  output MEMREAD,
  output MEMTOREG,
  output [2:0] ALU_OPERATION,
  output REG_WRITE,
  output [1:0] OPERAND_A_SEL,
  output OPERAND_B_SEL,
  output [1:0] EXTEND_SEL,
  output [1:0] NEXT_PC_SEL
);

  wire type_decode_1_branch, type_decode_1_i_type, type_decode_1_jal, type_decode_1_jalr, type_decode_1_load,
       type_decode_1_lui, type_decode_1_r_format, type_decode_1_store;

  TYPE_DECODE type_decode_1 (
    .OPCODE(OPCODE), .R_FORMAT(type_decode_1_r_format), .LOAD(type_decode_1_load),
    .STORE(type_decode_1_store), .BRANCH(type_decode_1_branch), .I_TYPE(type_decode_1_i_type),
    .JALR(type_decode_1_jalr), .JAL(type_decode_1_jal), .LUI(type_decode_1_lui));
  CONTROL_DECODE control_decode_1 (
    .MEMWRITE(MEM_WRITE), .BRANCH_2(BRANCH), .MEMREAD(MEMREAD), .MEMTOREG(MEMTOREG),
    .ALU_OPERATION(ALU_OPERATION), .REGWRITE(REG_WRITE), .OPERAND_A_SEL(OPERAND_A_SEL),
    .OPERAND_B_SEL(OPERAND_B_SEL), .EXTEND_SEL(EXTEND_SEL), .NEXT_PC_SELECT(NEXT_PC_SEL),
    .R_FORMAT(type_decode_1_r_format), .LOAD(type_decode_1_load), .STORE(type_decode_1_store),
    .BRANCH(type_decode_1_branch), .I_TYPE(type_decode_1_i_type), .JALR(type_decode_1_jalr),
    .JAL(type_decode_1_jal), .LUI(type_decode_1_lui));
endmodule

module TYPE_DECODE (
  input  [6:0] OPCODE,
  output R_FORMAT,
  output LOAD,
  output STORE,
  output BRANCH,
  output I_TYPE,
  output JALR,
  output JAL,
  output LUI
);

  Comparator #(.width(7)) comparator_1 (.a(OPCODE), .b(7'b0110011), .eq(R_FORMAT));  // open: gt, lt
  Comparator #(.width(7)) comparator_2 (.a(OPCODE), .b(7'b0000011), .eq(LOAD));  // open: gt, lt
  Comparator #(.width(7)) comparator_3 (.a(OPCODE), .b(7'b0100011), .eq(STORE));  // open: gt, lt
  Comparator #(.width(7)) comparator_4 (.a(OPCODE), .b(7'b1100011), .eq(BRANCH));  // open: gt, lt
  Comparator #(.width(7)) comparator_5 (.a(OPCODE), .b(7'b0010011), .eq(I_TYPE));  // open: gt, lt
  Comparator #(.width(7)) comparator_6 (.a(OPCODE), .b(7'b1100111), .eq(JALR));  // open: gt, lt
  Comparator #(.width(7)) comparator_7 (.a(OPCODE), .b(7'b1101111), .eq(JAL));  // open: gt, lt
  Comparator #(.width(7)) comparator_8 (.a(OPCODE), .b(7'b0110111), .eq(LUI));  // open: gt, lt
endmodule

module NEXT_PC_SELECT (
  input  BRANCH,
  input  JAL,
  input  JALR,
  output [1:0] OUTPUT
);

  wire and_1_out, and_2_out, and_3_out, and_4_out, not_1_out, not_2_out, not_3_out, not_4_out, not_5_out,
       not_6_out, not_7_out, not_8_out;

  not not_1 (not_1_out, BRANCH);
  not not_2 (not_2_out, JAL);
  not not_3 (not_3_out, BRANCH);
  not not_4 (not_4_out, JALR);
  not not_5 (not_5_out, BRANCH);
  not not_6 (not_6_out, JAL);
  not not_7 (not_7_out, JAL);
  not not_8 (not_8_out, JALR);
  and and_1 (and_1_out, not_1_out, not_2_out, JALR);
  and and_2 (and_2_out, not_3_out, JAL, not_4_out);
  and and_3 (and_3_out, not_5_out, not_6_out, JALR);
  and and_4 (and_4_out, BRANCH, not_7_out, not_8_out);
  or or_1 (OUTPUT[1], and_1_out, and_2_out);
  or or_2 (OUTPUT[0], and_3_out, and_4_out);
endmodule

module OPERAND_A_SEL (
  input  LUI,
  input  JAL,
  input  JALR,
  output [1:0] OUTPUT
);

  wire and_1_out, and_2_out, and_3_out, and_4_out, not_1_out, not_2_out, not_3_out, not_4_out, not_5_out,
       not_6_out, not_7_out, not_8_out;

  not not_1 (not_1_out, LUI);
  not not_2 (not_2_out, JAL);
  not not_3 (not_3_out, LUI);
  not not_4 (not_4_out, JALR);
  not not_5 (not_5_out, JAL);
  not not_6 (not_6_out, JALR);
  not not_7 (not_7_out, JAL);
  not not_8 (not_8_out, JALR);
  and and_1 (and_1_out, not_1_out, not_2_out, JALR);
  and and_2 (and_2_out, not_3_out, JAL, not_4_out);
  and and_3 (and_3_out, LUI, not_5_out, not_6_out);
  and and_4 (and_4_out, LUI, not_7_out, not_8_out);
  or or_1 (OUTPUT[0], and_1_out, and_2_out);
  or or_2 (OUTPUT[1], and_3_out, and_4_out);
endmodule

module ALU_OP (
  input  R_FORMAT,
  input  LOAD,
  input  STORE,
  input  BRANCH,
  input  I_TYPE,
  input  JALR,
  input  JAL,
  input  LUI,
  output [2:0] OUTPUT
);

  wire not_1_out, not_2_out, not_3_out, not_4_out, not_5_out, not_6_out, not_7_out, not_8_out, not_9_out,
       not_10_out, not_11_out, not_12_out, not_13_out;

  not not_1 (not_1_out, JALR);
  not not_2 (not_2_out, BRANCH);
  not not_3 (not_3_out, I_TYPE);
  not not_4 (not_4_out, JAL);
  not not_5 (not_5_out, R_FORMAT);
  not not_6 (not_6_out, R_FORMAT);
  not not_7 (not_7_out, LOAD);
  not not_8 (not_8_out, STORE);
  not not_9 (not_9_out, I_TYPE);
  not not_10 (not_10_out, R_FORMAT);
  not not_11 (not_11_out, LOAD);
  not not_12 (not_12_out, BRANCH);
  not not_13 (not_13_out, LUI);
  and and_1 (OUTPUT[2], not_5_out, not_2_out, not_3_out, not_1_out, not_4_out);
  and and_2 (OUTPUT[1], not_6_out, not_7_out, not_8_out, not_9_out);
  and and_3 (OUTPUT[0], not_10_out, not_11_out, not_12_out, not_13_out);
endmodule

module CONTROL_DECODE (
  input  R_FORMAT,
  input  LOAD,
  input  STORE,
  input  BRANCH,
  input  I_TYPE,
  input  JALR,
  input  JAL,
  input  LUI,
  output MEMWRITE,
  output BRANCH_2,
  output MEMREAD,
  output MEMTOREG,
  output [2:0] ALU_OPERATION,
  output REGWRITE,
  output [1:0] OPERAND_A_SEL,
  output OPERAND_B_SEL,
  output [1:0] EXTEND_SEL,
  output [1:0] NEXT_PC_SELECT
);

  or or_1 (REGWRITE, R_FORMAT, LOAD, I_TYPE, JALR, JAL, LUI);
  ALU_OP alu_op_1 (
    .R_FORMAT(R_FORMAT), .LOAD(LOAD), .STORE(STORE), .BRANCH(BRANCH), .I_TYPE(I_TYPE), .JALR(JALR),
    .JAL(JAL), .LUI(LUI), .OUTPUT(ALU_OPERATION));
  OPERAND_A_SEL operand_a_sel_1 (.LUI(LUI), .JAL(JAL), .JALR(JALR), .OUTPUT(OPERAND_A_SEL));
  or or_2 (OPERAND_B_SEL, LUI, I_TYPE, STORE, LOAD);
  NEXT_PC_SELECT next_pc_select_1 (.BRANCH(BRANCH), .JAL(JAL), .JALR(JALR), .OUTPUT(NEXT_PC_SELECT));

  assign BRANCH_2 = BRANCH;
  assign EXTEND_SEL = {STORE, LUI};
  assign MEMREAD = LOAD;
  assign MEMTOREG = LOAD;
  assign MEMWRITE = STORE;
endmodule

module CONTROL_UNIT (
  input  [6:0] OPCODE,
  output MEM_WRITE,
  output BRANCH,
  output MEM_READ,
  output MEM_TO_REG,
  output [2:0] ALU_OPERATION,
  output REG_WRITE,
  output [1:0] OPERAND_A_SEL,
  output OPERAND_B_SEL,
  output [1:0] EXTEND_SEL,
  output [1:0] NEXT_PC_SEL
);

  main main_1 (
    .OPCODE(OPCODE), .MEM_WRITE(MEM_WRITE), .BRANCH(BRANCH), .MEMREAD(MEM_READ), .MEMTOREG(MEM_TO_REG),
    .ALU_OPERATION(ALU_OPERATION), .REG_WRITE(REG_WRITE), .OPERAND_A_SEL(OPERAND_A_SEL),
    .OPERAND_B_SEL(OPERAND_B_SEL), .EXTEND_SEL(EXTEND_SEL), .NEXT_PC_SEL(NEXT_PC_SEL));
endmodule

module immediate_generation (
  input  [31:0] in_1,
  input  [31:0] in_2,
  output [31:0] out_3,
  output [31:0] out_4,
  output [31:0] out_5
);

  wire [31:0] bit_extender_2_out;

  assign out_3 = {{20{in_1[31]}}, {in_1[31:25], in_1[11:7]}};  // Bit_Extender bit_extender_1
  assign bit_extender_2_out = {{19{in_1[31]}}, {in_1[31], in_1[7], in_1[30:25], in_1[11:8], 1'b0}};  // Bit_Extender bit_extender_2
  assign out_5 = {{20{in_1[31]}}, in_1[31:20]};  // Bit_Extender bit_extender_3
  Adder #(.width(32)) adder_1 (.a(bit_extender_2_out), .b(in_2), .out(out_4));  // open: cin, cout

  // Notes on the sheet:
  //   INSTRUCTION
  //   PC
  //   S-Immediate
  //   SB-Immediate
  //   I-Immediate
endmodule

module _32_BIT_REG_FILE (
  input  [4:0] ReadReg1,
  input  [4:0] ReadReg2,
  input  [4:0] WriteReg,
  input  RegWrite,
  input  [31:0] WriteData,
  input  Clk,
  input  Reset,
  output [31:0] ReadData1,
  output [31:0] ReadData2
);

  wire decoder_1_out0, decoder_1_out1, decoder_2_out0, decoder_2_out1, decoder_2_out2, decoder_2_out3,
       decoder_3_out0, decoder_3_out1, decoder_3_out2, decoder_3_out3, decoder_4_out0, decoder_4_out1,
       decoder_4_out2, decoder_4_out3, decoder_5_out0, decoder_5_out1, decoder_5_out2, decoder_5_out3,
       decoder_6_out0, decoder_6_out1, decoder_6_out2, decoder_6_out3, decoder_7_out0, decoder_7_out1,
       decoder_7_out2, decoder_7_out3, decoder_8_out0, decoder_8_out1, decoder_8_out2, decoder_8_out3,
       decoder_9_out0, decoder_9_out1, decoder_9_out2, decoder_9_out3, decoder_10_out0, decoder_10_out1,
       decoder_10_out2, decoder_10_out3, decoder_11_out0, decoder_11_out1, decoder_11_out2, decoder_11_out3;
  wire [31:0] multiplexer_1_out, multiplexer_2_out, multiplexer_3_out, multiplexer_4_out, multiplexer_5_out,
       multiplexer_6_out, multiplexer_7_out, multiplexer_8_out, multiplexer_9_out, multiplexer_10_out,
       multiplexer_13_out, multiplexer_14_out, multiplexer_15_out, multiplexer_16_out, multiplexer_17_out,
       multiplexer_18_out, multiplexer_19_out, multiplexer_20_out, multiplexer_21_out, multiplexer_22_out,
       register_1_q, register_2_q, register_3_q, register_4_q, register_5_q, register_6_q, register_7_q,
       register_8_q, register_9_q, register_10_q, register_11_q, register_12_q, register_13_q, register_14_q,
       register_15_q, register_16_q, register_17_q, register_18_q, register_19_q, register_20_q,
       register_21_q, register_22_q, register_23_q, register_24_q, register_25_q, register_26_q,
       register_27_q, register_28_q, register_29_q, register_30_q, register_31_q;

  // Probe on WriteReg
  Decoder #(.disabled(0)) decoder_1 (.out0(decoder_1_out0), .out1(decoder_1_out1), .sel(WriteReg[4]), .en(RegWrite));
  Decoder #(.select(2), .disabled(0)) decoder_2 (
    .out0(decoder_2_out0), .out1(decoder_2_out1), .out2(decoder_2_out2), .out3(decoder_2_out3),
    .sel(WriteReg[3:2]), .en(decoder_1_out0));
  Decoder #(.select(2), .disabled(0)) decoder_3 (
    .out0(decoder_3_out0), .out1(decoder_3_out1), .out2(decoder_3_out2), .out3(decoder_3_out3),
    .sel(WriteReg[1:0]), .en(decoder_2_out0));
  Decoder #(.select(2), .disabled(0)) decoder_4 (
    .out0(decoder_4_out0), .out1(decoder_4_out1), .out2(decoder_4_out2), .out3(decoder_4_out3),
    .sel(WriteReg[1:0]), .en(decoder_2_out1));
  Decoder #(.select(2), .disabled(0)) decoder_5 (
    .out0(decoder_5_out0), .out1(decoder_5_out1), .out2(decoder_5_out2), .out3(decoder_5_out3),
    .sel(WriteReg[1:0]), .en(decoder_2_out2));
  Decoder #(.select(2), .disabled(0)) decoder_6 (
    .out0(decoder_6_out0), .out1(decoder_6_out1), .out2(decoder_6_out2), .out3(decoder_6_out3),
    .sel(WriteReg[1:0]), .en(decoder_2_out3));
  Register #(.width(32)) register_1 (.D(WriteData), .en(decoder_3_out1), .Q(register_1_q), .clk(Clk), .clr(Reset));
  Register #(.width(32)) register_2 (.D(WriteData), .en(decoder_3_out2), .Q(register_2_q), .clk(Clk), .clr(Reset));
  Register #(.width(32)) register_3 (.D(WriteData), .en(decoder_3_out3), .Q(register_3_q), .clk(Clk), .clr(Reset));
  Register #(.width(32)) register_4 (.D(WriteData), .en(decoder_4_out0), .Q(register_4_q), .clk(Clk), .clr(Reset));
  Register #(.width(32)) register_5 (.D(WriteData), .en(decoder_4_out1), .Q(register_5_q), .clk(Clk), .clr(Reset));
  Register #(.width(32)) register_6 (.D(WriteData), .en(decoder_4_out2), .Q(register_6_q), .clk(Clk), .clr(Reset));
  Register #(.width(32)) register_7 (.D(WriteData), .en(decoder_4_out3), .Q(register_7_q), .clk(Clk), .clr(Reset));
  Register #(.width(32)) register_8 (.D(WriteData), .en(decoder_5_out0), .Q(register_8_q), .clk(Clk), .clr(Reset));
  Register #(.width(32)) register_9 (.D(WriteData), .en(decoder_5_out1), .Q(register_9_q), .clk(Clk), .clr(Reset));
  Register #(.width(32)) register_10 (.D(WriteData), .en(decoder_5_out2), .Q(register_10_q), .clk(Clk), .clr(Reset));
  Register #(.width(32)) register_11 (.D(WriteData), .en(decoder_5_out3), .Q(register_11_q), .clk(Clk), .clr(Reset));
  Register #(.width(32)) register_12 (.D(WriteData), .en(decoder_6_out0), .Q(register_12_q), .clk(Clk), .clr(Reset));
  Register #(.width(32)) register_13 (.D(WriteData), .en(decoder_6_out1), .Q(register_13_q), .clk(Clk), .clr(Reset));
  Register #(.width(32)) register_14 (.D(WriteData), .en(decoder_6_out2), .Q(register_14_q), .clk(Clk), .clr(Reset));
  Register #(.width(32)) register_15 (.D(WriteData), .en(decoder_6_out3), .Q(register_15_q), .clk(Clk), .clr(Reset));
  // Probe on {32{1'b0}}
  // Probe on register_1_q
  // Probe on register_2_q
  // Probe on register_3_q
  // Probe on register_4_q
  // Probe on register_5_q
  // Probe on register_6_q
  // Probe on register_7_q
  // Probe on register_8_q
  // Probe on register_9_q
  // Probe on register_10_q
  // Probe on register_11_q
  // Probe on register_12_q
  // Probe on register_13_q
  // Probe on register_14_q
  // Probe on register_15_q
  // Probe on ReadReg1
  Multiplexer #(.select(2), .width(32), .enable("false")) multiplexer_1 (
    .in0({32{1'b0}}), .in1(register_1_q), .in2(register_2_q), .in3(register_3_q), .out(multiplexer_1_out),
    .sel(ReadReg1[1:0]));
  Multiplexer #(.select(2), .width(32), .enable("false")) multiplexer_2 (
    .in0(register_4_q), .in1(register_5_q), .in2(register_6_q), .in3(register_7_q), .out(multiplexer_2_out),
    .sel(ReadReg1[1:0]));
  Multiplexer #(.select(2), .width(32), .enable("false")) multiplexer_3 (
    .in0(register_8_q), .in1(register_9_q), .in2(register_10_q), .in3(register_11_q),
    .out(multiplexer_3_out), .sel(ReadReg1[1:0]));
  Multiplexer #(.select(2), .width(32), .enable("false")) multiplexer_4 (
    .in0(register_12_q), .in1(register_13_q), .in2(register_14_q), .in3(register_15_q),
    .out(multiplexer_4_out), .sel(ReadReg1[1:0]));
  // Probe on ReadReg2
  Multiplexer #(.select(2), .width(32), .enable("false")) multiplexer_5 (
    .in0({32{1'b0}}), .in1(register_1_q), .in2(register_2_q), .in3(register_3_q), .out(multiplexer_5_out),
    .sel(ReadReg2[1:0]));
  Multiplexer #(.select(2), .width(32), .enable("false")) multiplexer_6 (
    .in0(register_4_q), .in1(register_5_q), .in2(register_6_q), .in3(register_7_q), .out(multiplexer_6_out),
    .sel(ReadReg2[1:0]));
  Multiplexer #(.select(2), .width(32), .enable("false")) multiplexer_7 (
    .in0(register_8_q), .in1(register_9_q), .in2(register_10_q), .in3(register_11_q),
    .out(multiplexer_7_out), .sel(ReadReg2[1:0]));
  Multiplexer #(.select(2), .width(32), .enable("false")) multiplexer_8 (
    .in0(register_12_q), .in1(register_13_q), .in2(register_14_q), .in3(register_15_q),
    .out(multiplexer_8_out), .sel(ReadReg2[1:0]));
  Multiplexer #(.select(2), .width(32), .enable("false")) multiplexer_9 (
    .in0(multiplexer_5_out), .in1(multiplexer_6_out), .in2(multiplexer_7_out), .in3(multiplexer_8_out),
    .out(multiplexer_9_out), .sel(ReadReg2[3:2]));
  Multiplexer #(.select(2), .width(32), .enable("false")) multiplexer_10 (
    .in0(multiplexer_1_out), .in1(multiplexer_2_out), .in2(multiplexer_3_out), .in3(multiplexer_4_out),
    .out(multiplexer_10_out), .sel(ReadReg1[3:2]));
  Decoder #(.select(2), .disabled(0)) decoder_7 (
    .out0(decoder_7_out0), .out1(decoder_7_out1), .out2(decoder_7_out2), .out3(decoder_7_out3),
    .sel(WriteReg[3:2]), .en(decoder_1_out1));
  Decoder #(.select(2), .disabled(0)) decoder_8 (
    .out0(decoder_8_out0), .out1(decoder_8_out1), .out2(decoder_8_out2), .out3(decoder_8_out3),
    .sel(WriteReg[1:0]), .en(decoder_7_out0));
  Decoder #(.select(2), .disabled(0)) decoder_9 (
    .out0(decoder_9_out0), .out1(decoder_9_out1), .out2(decoder_9_out2), .out3(decoder_9_out3),
    .sel(WriteReg[1:0]), .en(decoder_7_out1));
  Decoder #(.select(2), .disabled(0)) decoder_10 (
    .out0(decoder_10_out0), .out1(decoder_10_out1), .out2(decoder_10_out2), .out3(decoder_10_out3),
    .sel(WriteReg[1:0]), .en(decoder_7_out2));
  Decoder #(.select(2), .disabled(0)) decoder_11 (
    .out0(decoder_11_out0), .out1(decoder_11_out1), .out2(decoder_11_out2), .out3(decoder_11_out3),
    .sel(WriteReg[1:0]), .en(decoder_7_out3));
  Register #(.width(32)) register_16 (.D(WriteData), .en(decoder_8_out0), .Q(register_16_q), .clk(Clk), .clr(Reset));
  Register #(.width(32)) register_17 (.D(WriteData), .en(decoder_8_out1), .Q(register_17_q), .clk(Clk), .clr(Reset));
  Register #(.width(32)) register_18 (.D(WriteData), .en(decoder_8_out2), .Q(register_18_q), .clk(Clk), .clr(Reset));
  Register #(.width(32)) register_19 (.D(WriteData), .en(decoder_8_out3), .Q(register_19_q), .clk(Clk), .clr(Reset));
  Register #(.width(32)) register_20 (.D(WriteData), .en(decoder_9_out0), .Q(register_20_q), .clk(Clk), .clr(Reset));
  Register #(.width(32)) register_21 (.D(WriteData), .en(decoder_9_out1), .Q(register_21_q), .clk(Clk), .clr(Reset));
  Register #(.width(32)) register_22 (.D(WriteData), .en(decoder_9_out2), .Q(register_22_q), .clk(Clk), .clr(Reset));
  Register #(.width(32)) register_23 (.D(WriteData), .en(decoder_9_out3), .Q(register_23_q), .clk(Clk), .clr(Reset));
  Register #(.width(32)) register_24 (.D(WriteData), .en(decoder_10_out0), .Q(register_24_q), .clk(Clk), .clr(Reset));
  Register #(.width(32)) register_25 (.D(WriteData), .en(decoder_10_out1), .Q(register_25_q), .clk(Clk), .clr(Reset));
  Register #(.width(32)) register_26 (.D(WriteData), .en(decoder_10_out2), .Q(register_26_q), .clk(Clk), .clr(Reset));
  Register #(.width(32)) register_27 (.D(WriteData), .en(decoder_10_out3), .Q(register_27_q), .clk(Clk), .clr(Reset));
  Register #(.width(32)) register_28 (.D(WriteData), .en(decoder_11_out0), .Q(register_28_q), .clk(Clk), .clr(Reset));
  Register #(.width(32)) register_29 (.D(WriteData), .en(decoder_11_out1), .Q(register_29_q), .clk(Clk), .clr(Reset));
  Register #(.width(32)) register_30 (.D(WriteData), .en(decoder_11_out2), .Q(register_30_q), .clk(Clk), .clr(Reset));
  Register #(.width(32)) register_31 (.D(WriteData), .en(decoder_11_out3), .Q(register_31_q), .clk(Clk), .clr(Reset));
  // Probe on register_16_q
  // Probe on register_17_q
  // Probe on register_18_q
  // Probe on register_19_q
  // Probe on register_20_q
  // Probe on register_21_q
  // Probe on register_22_q
  // Probe on register_23_q
  // Probe on register_24_q
  // Probe on register_25_q
  // Probe on register_26_q
  // Probe on register_27_q
  // Probe on register_28_q
  // Probe on register_29_q
  // Probe on register_30_q
  // Probe on register_31_q
  Multiplexer #(.width(32), .enable("false")) multiplexer_11 (
    .in0(multiplexer_10_out), .in1(multiplexer_22_out), .out(ReadData1), .sel(ReadReg1[4]));
  Multiplexer #(.width(32), .enable("false")) multiplexer_12 (
    .in0(multiplexer_9_out), .in1(multiplexer_21_out), .out(ReadData2), .sel(ReadReg2[4]));
  Multiplexer #(.select(2), .width(32), .enable("false")) multiplexer_13 (
    .in0(register_16_q), .in1(register_17_q), .in2(register_18_q), .in3(register_19_q),
    .out(multiplexer_13_out), .sel(ReadReg1[1:0]));
  Multiplexer #(.select(2), .width(32), .enable("false")) multiplexer_14 (
    .in0(register_20_q), .in1(register_21_q), .in2(register_22_q), .in3(register_23_q),
    .out(multiplexer_14_out), .sel(ReadReg1[1:0]));
  Multiplexer #(.select(2), .width(32), .enable("false")) multiplexer_15 (
    .in0(register_24_q), .in1(register_25_q), .in2(register_26_q), .in3(register_27_q),
    .out(multiplexer_15_out), .sel(ReadReg1[1:0]));
  Multiplexer #(.select(2), .width(32), .enable("false")) multiplexer_16 (
    .in0(register_28_q), .in1(register_29_q), .in2(register_30_q), .in3(register_31_q),
    .out(multiplexer_16_out), .sel(ReadReg1[1:0]));
  Multiplexer #(.select(2), .width(32), .enable("false")) multiplexer_17 (
    .in0(register_16_q), .in1(register_17_q), .in2(register_18_q), .in3(register_19_q),
    .out(multiplexer_17_out), .sel(ReadReg2[1:0]));
  Multiplexer #(.select(2), .width(32), .enable("false")) multiplexer_18 (
    .in0(register_20_q), .in1(register_21_q), .in2(register_22_q), .in3(register_23_q),
    .out(multiplexer_18_out), .sel(ReadReg2[1:0]));
  Multiplexer #(.select(2), .width(32), .enable("false")) multiplexer_19 (
    .in0(register_24_q), .in1(register_25_q), .in2(register_26_q), .in3(register_27_q),
    .out(multiplexer_19_out), .sel(ReadReg2[1:0]));
  Multiplexer #(.select(2), .width(32), .enable("false")) multiplexer_20 (
    .in0(register_28_q), .in1(register_29_q), .in2(register_30_q), .in3(register_31_q),
    .out(multiplexer_20_out), .sel(ReadReg2[1:0]));
  Multiplexer #(.select(2), .width(32), .enable("false")) multiplexer_21 (
    .in0(multiplexer_17_out), .in1(multiplexer_18_out), .in2(multiplexer_19_out), .in3(multiplexer_20_out),
    .out(multiplexer_21_out), .sel(ReadReg2[3:2]));
  Multiplexer #(.select(2), .width(32), .enable("false")) multiplexer_22 (
    .in0(multiplexer_13_out), .in1(multiplexer_14_out), .in2(multiplexer_15_out), .in3(multiplexer_16_out),
    .out(multiplexer_22_out), .sel(ReadReg1[3:2]));
endmodule

module RV_32I (
  input  CLEAR,
  output OVERFLOW
);

  wire alucontrol_and_alu_1_branch, and_1_out, clock_1_out, main_1_branch, main_1_mem_write, main_1_memread,
       main_1_memtoreg, main_1_operand_b_sel, main_1_reg_write;
  wire [1:0] main_1_extend_sel, main_1_next_pc_sel;
  wire [2:0] main_1_alu_operation, rom_1_data_3;
  wire [4:0] rom_1_data_4;
  wire [6:0] rom_1_data;
  wire [7:0] alucontrol_and_alu_1_output_2;
  wire [19:0] PC_q_2;
  wire [31:0] adder_1_out, alucontrol_and_alu_1_output, immediate_generation_1_out_3,
       immediate_generation_1_out_4, immediate_generation_1_out_5, multiplexer_1_out, multiplexer_2_out,
       multiplexer_3_out, multiplexer_4_out, multiplexer_5_out, n32_bit_reg_file_1_readdata1,
       n32_bit_reg_file_1_readdata2, PC_q, ram_1_data;
  wire [31:7] rom_1_data_2;

  Clock clock_1 (.out(clock_1_out));
  // Probe on multiplexer_1_out
  // Probe on immediate_generation_1_out_4
  Register #(.width(32)) PC (
    .D(multiplexer_1_out), .Q({PC_q[31:22], PC_q_2, PC_q[1:0]}), .clk(clock_1_out), .clr(CLEAR));  // open: en
  Adder #(.width(32)) adder_1 (.a({PC_q[31:22], PC_q_2, PC_q[1:0]}), .b(32'h4), .out(adder_1_out));  // open: cin, cout
  // Probe on rom_1_data_2[30]
  // Probe on rom_1_data_3
  Multiplexer #(.select(2), .width(32)) multiplexer_1 (
    .in0(adder_1_out), .in1(multiplexer_2_out), .out(multiplexer_1_out), .sel(main_1_next_pc_sel));  // open: in2, in3, en
  // Probe on multiplexer_1_out
  // Probe on rom_1_data
  ROM #(.addrWidth(20), .dataWidth(32)) rom_1 (
    .addr(PC_q_2),
    .data({rom_1_data_2[31:25], rom_1_data_4, rom_1_data_2[19:15], rom_1_data_3, rom_1_data_2[11:7], rom_1_data}));  // open: sel
  // Probe on rom_1_data_2[11:7]
  // Probe on rom_1_data_2[19:15]
  // Probe on rom_1_data_4
  // Probe on rom_1_data_2[25]
  // Probe on main_1_next_pc_sel
  Multiplexer #(.width(32)) multiplexer_2 (
    .in0(adder_1_out), .in1(immediate_generation_1_out_4), .out(multiplexer_2_out), .sel(and_1_out));  // open: en
  _32_BIT_REG_FILE u_32_bit_reg_file_1 (
    .ReadReg1(rom_1_data_2[19:15]), .ReadReg2(rom_1_data_4), .WriteReg(rom_1_data_2[11:7]),
    .RegWrite(main_1_reg_write), .WriteData(multiplexer_5_out), .Clk(clock_1_out),
    .ReadData1(n32_bit_reg_file_1_readdata1), .ReadData2(n32_bit_reg_file_1_readdata2), .Reset(CLEAR));
  immediate_generation immediate_generation_1 (
    .out_3(immediate_generation_1_out_3),
    .in_1({rom_1_data_2[31:25], rom_1_data_4, rom_1_data_2[19:15], rom_1_data_3, rom_1_data_2[11:7], rom_1_data}),
    .out_4(immediate_generation_1_out_4), .in_2({PC_q[31:22], PC_q_2, PC_q[1:0]}),
    .out_5(immediate_generation_1_out_5));
  main main_1 (
    .OPCODE(rom_1_data), .MEM_WRITE(main_1_mem_write), .BRANCH(main_1_branch), .MEMREAD(main_1_memread),
    .MEMTOREG(main_1_memtoreg), .ALU_OPERATION(main_1_alu_operation), .REG_WRITE(main_1_reg_write),
    .OPERAND_B_SEL(main_1_operand_b_sel), .EXTEND_SEL(main_1_extend_sel), .NEXT_PC_SEL(main_1_next_pc_sel));  // open: OPERAND_A_SEL
  // Probe on multiplexer_5_out
  // Probe on main_1_alu_operation
  Multiplexer #(.width(32)) multiplexer_3 (
    .in0(n32_bit_reg_file_1_readdata2), .in1(multiplexer_4_out), .out(multiplexer_3_out),
    .sel(main_1_operand_b_sel));  // open: en
  Multiplexer #(.select(2), .width(32)) multiplexer_4 (
    .in0(immediate_generation_1_out_5), .in2(immediate_generation_1_out_3), .out(multiplexer_4_out),
    .sel(main_1_extend_sel));  // open: in1, in3, en
  // Probe on multiplexer_4_out
  and and_1 (and_1_out, alucontrol_and_alu_1_branch, main_1_branch);
  // Probe on n32_bit_reg_file_1_readdata1
  // Probe on multiplexer_3_out
  alucontrol_and_alu alucontrol_and_alu_1 (
    .ALU_OP(main_1_alu_operation), .FUNCT_3(rom_1_data_3), .FUNCT_7(rom_1_data_2[30]),
    .OPERAND_A(n32_bit_reg_file_1_readdata1), .OPERAND_B(multiplexer_3_out), .out_7(OVERFLOW),
    .OUTPUT({alucontrol_and_alu_1_output[31:10], alucontrol_and_alu_1_output_2, alucontrol_and_alu_1_output[1:0]}),
    .BRANCH(alucontrol_and_alu_1_branch), .FUNCT_7__25TH_BIT(rom_1_data_2[25]));
  // Probe on {alucontrol_and_alu_1_output[31:10], alucontrol_and_alu_1_output_2, alucontrol_and_alu_1_output[1:0]}
  RAM #(.dataWidth(32), .bus("separate")) ram_1 (
    .addr(alucontrol_and_alu_1_output_2), .din(n32_bit_reg_file_1_readdata2), .data(ram_1_data),
    .str(main_1_mem_write), .clk(clock_1_out), .ld(main_1_memread), .clr(CLEAR));  // open: sel
  // Probe on ram_1_data
  Multiplexer #(.width(32)) multiplexer_5 (
    .in0({alucontrol_and_alu_1_output[31:10], alucontrol_and_alu_1_output_2, alucontrol_and_alu_1_output[1:0]}),
    .in1(ram_1_data), .out(multiplexer_5_out), .sel(main_1_memtoreg));  // open: en

  // Notes on the sheet:
  //   contents of rom_1 (hex, n*v repeats v):
  //   2083 402103 802183 400213 2210133 23081b3 2320233 40410133 10663 2014063 204863 100293 502023 c63
  //   200293 502023 663 293 502023
  //   KINZA QAMAR ZAMAN (18B 58 CE)
endmodule

module alucontrol_and_alu (
  input  [2:0] ALU_OP,
  input  [2:0] FUNCT_3,
  input  FUNCT_7,
  input  FUNCT_7__25TH_BIT,
  input  [31:0] OPERAND_A,
  input  [31:0] OPERAND_B,
  output out_7,
  output [31:0] OUTPUT,
  output BRANCH
);

  wire adder_1_cout, comparator_1_eq, comparator_2_eq, comparator_3_eq, comparator_3_gt, comparator_3_lt,
       comparator_4_eq, comparator_4_gt, comparator_4_lt, comparator_5_lt, comparator_6_lt, decoder_1_out0,
       decoder_1_out1, decoder_1_out2, decoder_1_out4, decoder_1_out5, demultiplexer_1_out0,
       demultiplexer_1_out1, multiplexer_14_out, not_1_out, or_1_out, or_2_out, subtractor_1_bout;
  wire [2:0] multiplexer_1_out, multiplexer_2_out, multiplexer_3_out, multiplexer_4_out, multiplexer_5_out,
       multiplexer_8_out, multiplexer_9_out, priority_encoder_1_p4;
  wire [4:0] multiplexer_7_out;
  wire [26:0] multiplexer_7_out_2;
  wire [31:0] adder_1_out, adder_2_out, and_2_out, bit_extender_1_out, bit_extender_2_out,
       bit_extender_3_out, bit_extender_4_out, multiplexer_6_out, multiplexer_10_out, multiplexer_11_out,
       multiplexer_12_out, multiplexer_13_out, multiplexer_15_out, multiplexer_16_out, multiplexer_17_out,
       multiplexer_18_out, multiplexer_19_out, multiplexer_20_out, multiplexer_21_out, multiplier_1_out,
       or_3_out, shifter_1_out, shifter_2_out, shifter_3_out, subtractor_1_out, xor_1_out;

  Decoder #(.select(3)) decoder_1 (
    .out0(decoder_1_out0), .out1(decoder_1_out1), .out2(decoder_1_out2), .out4(decoder_1_out4),
    .out5(decoder_1_out5), .sel(ALU_OP));  // open: out3, out6, out7, en
  // Priority_Encoder priority_encoder_1: pin names not known; wires that end beside it: decoder_1_out0, decoder_1_out1, decoder_1_out2, priority_encoder_1_p4, decoder_1_out4, decoder_1_out5
  Comparator #(.width(2)) comparator_1 (.a(ALU_OP[1:0]), .b(2'b10), .eq(comparator_1_eq));  // open: gt, lt
  Comparator #(.width(32)) comparator_2 (.a(32'h1), .b(OUTPUT), .eq(comparator_2_eq));  // open: gt, lt
  Multiplexer #(.width(3)) multiplexer_1 (
    .in0(FUNCT_3), .in1(FUNCT_3), .out(multiplexer_1_out), .sel(ALU_OP[2]), .en(decoder_1_out0));
  Multiplexer #(.width(3)) multiplexer_2 (
    .in0(FUNCT_3), .in1(FUNCT_3), .out(multiplexer_2_out), .sel(ALU_OP[2]), .en(decoder_1_out1));
  Multiplexer #(.width(3)) multiplexer_3 (
    .in0(FUNCT_3), .in1(FUNCT_3), .out(multiplexer_3_out), .sel(ALU_OP[2]), .en(decoder_1_out2));
  Multiplexer #(.width(3)) multiplexer_4 (
    .in0(FUNCT_3), .in1(FUNCT_3), .out(multiplexer_4_out), .sel(ALU_OP[2]), .en(decoder_1_out4));
  Multiplexer #(.width(3)) multiplexer_5 (
    .in0(FUNCT_3), .in1(FUNCT_3), .out(multiplexer_5_out), .sel(ALU_OP[2]), .en(decoder_1_out5));
  Multiplexer #(.width(32)) multiplexer_6 (
    .in0(OPERAND_A), .in1(OPERAND_A), .out(multiplexer_6_out), .sel(ALU_OP[0]));  // open: en
  Multiplexer #(.width(32)) multiplexer_7 (
    .in0(OPERAND_B), .in1(OPERAND_B), .out({multiplexer_7_out_2, multiplexer_7_out}), .sel(ALU_OP[0]));  // open: en
  Multiplexer #(.width(3)) multiplexer_8 (
    .in0(multiplexer_1_out), .in1(multiplexer_2_out), .out(multiplexer_8_out), .sel(ALU_OP[0]));  // open: en
  Multiplexer #(.width(3)) multiplexer_9 (
    .in0(multiplexer_4_out), .in1(multiplexer_5_out), .out(multiplexer_9_out), .sel(ALU_OP[0]));  // open: en
  and and_1 (BRANCH, comparator_1_eq, comparator_2_eq);
  Multiplexer #(.select(3), .width(32)) multiplexer_10 (
    .in0(OPERAND_A), .in1(OPERAND_A), .in2(OPERAND_A), .in3(OPERAND_A), .in4(OPERAND_A), .in5(OPERAND_A),
    .in6(OPERAND_A), .out(multiplexer_10_out), .sel(multiplexer_9_out));  // open: in7, en
  Multiplexer #(.select(3), .width(32)) multiplexer_11 (
    .in0(OPERAND_B), .in1(OPERAND_B), .in2(OPERAND_B), .in3(OPERAND_B), .in4(OPERAND_B), .in5(OPERAND_B),
    .in6(OPERAND_B), .out(multiplexer_11_out), .sel(multiplexer_9_out));  // open: in7, en
  Comparator #(.width(32)) comparator_3 (
    .a(OPERAND_A), .b(OPERAND_B), .gt(comparator_3_gt), .eq(comparator_3_eq), .lt(comparator_3_lt));
  Comparator #(.width(32), .mode("unsigned")) comparator_4 (
    .a(OPERAND_A), .b(OPERAND_B), .gt(comparator_4_gt), .eq(comparator_4_eq), .lt(comparator_4_lt));
  Demultiplexer demultiplexer_1 (
    .out0(demultiplexer_1_out0), .out1(demultiplexer_1_out1), .in(FUNCT_7), .sel(ALU_OP[0]));  // open: en
  or or_1 (or_1_out, comparator_3_eq, comparator_3_gt);
  assign bit_extender_1_out = {{31{1'b0}}, comparator_3_lt};  // Bit_Extender bit_extender_1
  or or_2 (or_2_out, comparator_4_gt, comparator_4_eq);
  not not_1 (not_1_out, comparator_4_eq);
  Multiplexer #(.width(32)) multiplexer_12 (
    .in0({32{1'b0}}), .in1(32'h1), .out(multiplexer_12_out), .sel(or_1_out));  // open: en
  Multiplexer #(.width(32)) multiplexer_13 (
    .in0({32{1'b0}}), .in1(32'h1), .out(multiplexer_13_out), .sel(or_2_out));  // open: en
  Multiplexer multiplexer_14 (
    .in0(demultiplexer_1_out0), .in1(demultiplexer_1_out1), .out(multiplexer_14_out), .sel(ALU_OP[0]));  // open: en
  assign bit_extender_2_out = {{31{1'b0}}, comparator_4_lt};  // Bit_Extender bit_extender_2
  Multiplexer #(.width(32)) multiplexer_15 (
    .in0({32{1'b0}}), .in1(32'h1), .out(multiplexer_15_out), .sel(comparator_3_eq));  // open: en
  Adder #(.width(32)) adder_1 (
    .a(multiplexer_6_out), .b({multiplexer_7_out_2, multiplexer_7_out}), .out(adder_1_out),
    .cout(adder_1_cout));  // open: cin
  Subtractor #(.width(32)) subtractor_1 (
    .a(multiplexer_6_out), .b({multiplexer_7_out_2, multiplexer_7_out}), .out(subtractor_1_out),
    .bout(subtractor_1_bout));  // open: bin
  Multiplexer #(.width(32)) multiplexer_16 (
    .in0({32{1'b0}}), .in1(32'h1), .out(multiplexer_16_out), .sel(not_1_out));  // open: en
  Shifter #(.width(32)) shifter_1 (.in(multiplexer_6_out), .\dist (multiplexer_7_out), .out(shifter_1_out));
  Comparator #(.width(32)) comparator_5 (
    .a(multiplexer_6_out), .b({multiplexer_7_out_2, multiplexer_7_out}), .lt(comparator_5_lt));  // open: gt, eq
  Comparator #(.width(32), .mode("unsigned")) comparator_6 (
    .a(multiplexer_6_out), .b({multiplexer_7_out_2, multiplexer_7_out}), .lt(comparator_6_lt));  // open: gt, eq
  assign xor_1_out = multiplexer_6_out ^ {multiplexer_7_out_2, multiplexer_7_out};  // XOR_Gate xor_1, 32 bits wide
  Shifter #(.width(32), .shift("lr")) shifter_2 (
    .in(multiplexer_6_out), .\dist (multiplexer_7_out), .out(shifter_2_out));
  Shifter #(.width(32), .shift("ar")) shifter_3 (
    .in(multiplexer_6_out), .\dist (multiplexer_7_out), .out(shifter_3_out));
  assign or_3_out = multiplexer_6_out | {multiplexer_7_out_2, multiplexer_7_out};  // OR_Gate or_3, 32 bits wide
  assign and_2_out = multiplexer_6_out & {multiplexer_7_out_2, multiplexer_7_out};  // AND_Gate and_2, 32 bits wide
  Adder #(.width(32)) adder_2 (.a(multiplexer_10_out), .b(multiplexer_11_out), .out(adder_2_out));  // open: cin, cout
  Multiplier #(.width(32)) multiplier_1 (
    .a(multiplexer_6_out), .b({multiplexer_7_out_2, multiplexer_7_out}), .out(multiplier_1_out));  // open: cin, cout
  Multiplexer #(.width(32)) multiplexer_17 (
    .in0(adder_1_out), .in1(subtractor_1_out), .out(multiplexer_17_out), .sel(demultiplexer_1_out0), .en(1'b1));
  assign bit_extender_3_out = {{31{comparator_5_lt}}, comparator_5_lt};  // Bit_Extender bit_extender_3
  assign bit_extender_4_out = {{31{1'b0}}, comparator_6_lt};  // Bit_Extender bit_extender_4
  Multiplexer #(.width(32)) multiplexer_18 (
    .in0(shifter_2_out), .in1(shifter_3_out), .out(multiplexer_18_out), .sel(multiplexer_14_out), .en(1'b1));
  Multiplexer #(.select(3), .width(32)) multiplexer_19 (
    .in0(multiplexer_15_out), .in1(multiplexer_16_out), .in4(bit_extender_1_out), .in5(multiplexer_12_out),
    .in6(bit_extender_2_out), .in7(multiplexer_13_out), .out(multiplexer_19_out), .sel(multiplexer_3_out));  // open: in2, in3, en
  Multiplexer #(.width(32)) multiplexer_20 (
    .in0(multiplexer_17_out), .in1(multiplier_1_out), .out(multiplexer_20_out), .sel(FUNCT_7__25TH_BIT));  // open: en
  or or_4 (out_7, adder_1_cout, subtractor_1_bout);
  Multiplexer #(.select(3), .width(32)) multiplexer_21 (
    .in0(multiplexer_20_out), .in1(shifter_1_out), .in2(bit_extender_3_out), .in3(bit_extender_4_out),
    .in4(xor_1_out), .in5(multiplexer_18_out), .in6(or_3_out), .in7(and_2_out), .out(multiplexer_21_out),
    .sel(multiplexer_8_out));  // open: en
  Multiplexer #(.select(3), .width(32)) multiplexer_22 (
    .in0(multiplexer_21_out), .in1(multiplexer_21_out), .in2(multiplexer_19_out), .in4(adder_2_out),
    .in5(adder_2_out), .out(OUTPUT), .sel(priority_encoder_1_p4));  // open: in3, in6, in7, en
endmodule
